// Logisim project TinyCPU.circ as structural Verilog: 5 circuits, main circuit TinyCPU
module TinyCPU (
);

  Datapath datapath_1 ();  // open: DATA_IN, ACC_LOAD, VALID_IN, CLK, ACC_OUT, ACC_VALID_OUT, ZERO, NEGATIVE
  AddressPath addresspath_1 ();  // open: ADDRESS_IN, OFFSET, AR_LOAD, VALID_IN, CLK, ADDRESS, ADDRESS_VALID, ADDRESS_PLUS_OFFSET, OFFSET_CARRY
  Memory memory_1 ();  // open: ADDRESS, DATA_IN, VALID_IN, WRITE_ENABLE, CLK, DATA_OUT, VALID_OUT
  ErrorFlags errorflags_1 ();  // open: CLEAR_ERROR, CLK, SET_OVF, SET_DIV0, SET_ADDR, SET_INV, SET_ILL, SET_INPUT, OVF_OUT, DIV0_OUT, ADDR_OUT, INV_OUT, ILL_OUT, INPUT_OUT

  // Notes on the sheet:
  //   TinyCPU 16/12 starter — wire and verify each subcircuit before adding control logic
endmodule

module Datapath (
  input  [15:0] DATA_IN,
  input  ACC_LOAD,
  input  VALID_IN,
  input  CLK,
  output [15:0] ACC_OUT,
  output ACC_VALID_OUT,
  output ZERO,
  output NEGATIVE
);

  wire undriven;

  Register #(.width(16)) ACC (.D(DATA_IN), .Q(ACC_OUT), .clk(undriven));  // open: en, clr
  Register #(.width(1)) ACC_VALID (.D(VALID_IN), .Q(ACC_VALID_OUT), .clk(undriven));  // open: en, clr
  Comparator #(.mode("twosComplement"), .width(16)) ACC_STATUS (
    .a(ACC_OUT), .b({16{1'b0}}), .eq(ZERO), .lt(NEGATIVE));  // open: gt

  // Notes on the sheet:
  //   Clocked 16-bit accumulator; signed comparator derives ZERO and NEGATIVE
endmodule

module AddressPath (
  input  [11:0] ADDRESS_IN,
  input  [11:0] OFFSET,
  input  AR_LOAD,
  input  VALID_IN,
  input  CLK,
  output [11:0] ADDRESS,
  output ADDRESS_VALID,
  output [11:0] ADDRESS_PLUS_OFFSET,
  output OFFSET_CARRY
);

  Register #(.width(12)) AR (.D(ADDRESS_IN), .Q(ADDRESS), .clk(AR_LOAD));  // open: en, clr
  Register #(.width(1)) AR_VALID (.D(VALID_IN), .Q(ADDRESS_VALID), .clk(AR_LOAD));  // open: en, clr
  // Adder #(.width(12)) OFFSET_ADDER: pin names not known; wires that end beside it: ADDRESS, OFFSET, ADDRESS_PLUS_OFFSET, OFFSET_CARRY

  // Notes on the sheet:
  //   Clocked 12-bit address register with combinational offset addition
endmodule

module Memory (
  input  [11:0] ADDRESS,
  input  [15:0] DATA_IN,
  input  VALID_IN,
  input  WRITE_ENABLE,
  input  CLK,
  output [15:0] DATA_OUT,
  output VALID_OUT
);

  wire DATA_RAM_p2, DATA_RAM_p3, DATA_RAM_p10;

  // RAM #(.addrWidth(12), .dataWidth(16)) DATA_RAM: pin names not known; wires that end beside it: DATA_IN, DATA_RAM_p2, DATA_RAM_p3, ADDRESS, VALID_IN, DATA_RAM_p2, DATA_RAM_p3, DATA_OUT, VALID_OUT, DATA_RAM_p10
  // RAM #(.addrWidth(12), .dataWidth(1)) VALID_RAM: pin names not known; wires that end beside it: VALID_IN, DATA_RAM_p2, DATA_RAM_p3, VALID_OUT, DATA_RAM_p10

  // Notes on the sheet:
  //   4096-word value/valid memory with shared address, write-enable, and clock
endmodule

module ErrorFlags (
  input  CLEAR_ERROR,
  input  CLK,
  input  SET_OVF,
  input  SET_DIV0,
  input  SET_ADDR,
  input  SET_INV,
  input  SET_ILL,
  input  SET_INPUT,
  output OVF_OUT,
  output DIV0_OUT,
  output ADDR_OUT,
  output INV_OUT,
  output ILL_OUT,
  output INPUT_OUT
);

  wire HOLD_ADDR_p2, HOLD_DIV0_p2, HOLD_ILL_p2, HOLD_INPUT_p2, HOLD_INV_p2, HOLD_OVF_p2, NEXT_ADDR_out,
       NEXT_DIV0_out, NEXT_ILL_out, NEXT_INPUT_out, NEXT_INV_out, NEXT_OVF_out, NOT_CLEAR_ERROR_out;

  not NOT_CLEAR_ERROR (NOT_CLEAR_ERROR_out, CLEAR_ERROR);
  // AND_Gate HOLD_OVF: pin names not known; wires that end beside it: NOT_CLEAR_ERROR_out, HOLD_OVF_p2
  // AND_Gate HOLD_DIV0: pin names not known; wires that end beside it: NOT_CLEAR_ERROR_out, HOLD_DIV0_p2
  // AND_Gate HOLD_ADDR: pin names not known; wires that end beside it: NOT_CLEAR_ERROR_out, HOLD_ADDR_p2
  // AND_Gate HOLD_INV: pin names not known; wires that end beside it: NOT_CLEAR_ERROR_out, HOLD_INV_p2
  // AND_Gate HOLD_ILL: pin names not known; wires that end beside it: NOT_CLEAR_ERROR_out, HOLD_ILL_p2
  // AND_Gate HOLD_INPUT: pin names not known; wires that end beside it: NOT_CLEAR_ERROR_out, HOLD_INPUT_p2
  or NEXT_OVF (NEXT_OVF_out, SET_OVF, HOLD_OVF_p2);
  or NEXT_DIV0 (NEXT_DIV0_out, SET_DIV0, HOLD_DIV0_p2);
  or NEXT_ADDR (NEXT_ADDR_out, SET_ADDR, HOLD_ADDR_p2);
  or NEXT_INV (NEXT_INV_out, SET_INV, HOLD_INV_p2);
  or NEXT_ILL (NEXT_ILL_out, SET_ILL, HOLD_ILL_p2);
  or NEXT_INPUT (NEXT_INPUT_out, SET_INPUT, HOLD_INPUT_p2);
  // Register #(.width(1)) OVF: pin names not known; wires that end beside it: NEXT_OVF_out, NEXT_DIV0_out, OVF_OUT, DIV0_OUT, NOT_CLEAR_ERROR_out, NOT_CLEAR_ERROR_out
  // Register #(.width(1)) DIV0: pin names not known; wires that end beside it: NEXT_DIV0_out, NEXT_ADDR_out, ADDR_OUT, NOT_CLEAR_ERROR_out, NOT_CLEAR_ERROR_out
  // Register #(.width(1)) ADDR: pin names not known; wires that end beside it: NEXT_ADDR_out, NEXT_INV_out, INV_OUT, NOT_CLEAR_ERROR_out, NOT_CLEAR_ERROR_out
  // Register #(.width(1)) INV: pin names not known; wires that end beside it: NEXT_INV_out, NEXT_ILL_out, ILL_OUT, NOT_CLEAR_ERROR_out, NOT_CLEAR_ERROR_out
  // Register #(.width(1)) ILL: pin names not known; wires that end beside it: NEXT_ILL_out, NEXT_INPUT_out, INPUT_OUT, NOT_CLEAR_ERROR_out, NOT_CLEAR_ERROR_out
  // Register #(.width(1)) INPUT: pin names not known; wires that end beside it: NEXT_INPUT_out, NOT_CLEAR_ERROR_out

  // Notes on the sheet:
  //   Set-dominant sticky flags: SET OR (current AND NOT CLEAR_ERROR)
endmodule
